# Fritzing sketch WaterCounter (saved by Fritzing 0.9.3b)
circuit board: 7cm x 5cm
breadboards: 1

parts:
  WeMos_D1_Mini1 = WeMos D1 Mini
  TSP-03 = HLK-PM01
  220V = screw terminal, 2 pins
  Cold = screw terminal, 2 pins
  Hot = screw terminal, 2 pins
  Alarm = screw terminal, 3 pins
  Blue = LED - 5mm [color="Blue (525nm)" package="5 mm [THT]"]
  Red = LED - 5mm [color="Red (633nm)" package="5 mm [THT]"]
  220 = Resistor [tolerance=±5% resistance=220 package=THT]
  220_2 = Resistor [tolerance=±5% resistance=220 package=THT]
  10K = Resistor [tolerance=±5% resistance=10k package=THT]
  10K_2 = Resistor [tolerance=±5% resistance=10k package=THT]
  3_3v = Pad [width=2 height=2 connect=center]
  5v = Pad [width=2 height=2 connect=center]
  part = Pad [width=2 height=2 connect=center]

nets:
  3.3V: WeMos_D1_Mini1.3V3, TSP-03.+Vo, 3_3v.pad, part.pad
  5V: WeMos_D1_Mini1.5V, 5v.pad
  N1: WeMos_D1_Mini1.D2, Hot.pin1
  N2: WeMos_D1_Mini1.D5, Cold.pin1
  N3: WeMos_D1_Mini1.D6, Alarm.pin1
  N4: WeMos_D1_Mini1.D7, Blue.anode, 10K.Pin_0
  N5: WeMos_D1_Mini1.D8, Red.anode, 10K_2.Pin_0
  GND: WeMos_D1_Mini1.G, TSP-03.-Vo, Cold.pin2, Hot.pin2, Alarm.pin2, 220.Pin_0, 220_2.Pin_0, 10K.Pin_1, 10K_2.Pin_1
  N6: TSP-03.AC#0, 220V.pin2
  N7: TSP-03.AC#1, 220V.pin1
  N8: Blue.cathode, 220.Pin_1
  N9: Red.cathode, 220_2.Pin_1

notes:
  Vadim Babajanyan
  rev. 1.1
  15.06.2017
  Water Counter
  3.3V
  5V
  1.1
